// Logisim project Processador-MINIPS.circ as structural Verilog: 4 circuits, main circuit main
module main (
  input  CLEAR,
  output [7:0] out_2
);

  wire CLK_out;
  wire [1:0] multiplexer_1_out;
  wire [5:0] controle_1_sinal_de_controle;
  wire [7:0] adder_1_out, multiplexer_2_out, multiplexer_3_out, PC_q, regs_1_dr1, regs_1_dr2, ula_1_out_4;

  Clock CLK (.out(CLK_out));
  RAM #(.Select("low")) ram_1 (.addr(PC_q), .data(out_2), .clk(CLK_out));  // open: sel, ld, clr
  Adder adder_1 (.a(PC_q), .b(8'h1), .out(adder_1_out));  // open: cin, cout
  Controle controle_1 (.opcode(out_2[7:4]), .Sinal_de_controle(controle_1_sinal_de_controle));
  Register #(.Select("low")) PC (.D(adder_1_out), .Q(PC_q), .clk(CLK_out), .clr(CLEAR));  // open: en
  Multiplexer #(.width(2), .enable("false")) multiplexer_1 (
    .in0(out_2[3:2]), .in1(2'b00), .out(multiplexer_1_out), .sel(controle_1_sinal_de_controle[1]));
  Regs regs_1 (
    .dRW(multiplexer_3_out), .rw(controle_1_sinal_de_controle[2]), .RW_2(2'b00), .CLK(CLK_out),
    .R1(multiplexer_1_out), .R2(out_2[1:0]), .dR1(regs_1_dr1), .dR2(regs_1_dr2));
  Multiplexer #(.width(8), .enable("false")) multiplexer_2 (
    .in0(regs_1_dr2), .in1({4'b0000, out_2[3:0]}), .out(multiplexer_2_out),
    .sel(controle_1_sinal_de_controle[1]));
  ULA ula_1 (.DA(regs_1_dr1), .DB(multiplexer_2_out), .out_4(ula_1_out_4), .Sel(controle_1_sinal_de_controle[5:3]));
  Multiplexer #(.width(8), .enable("false")) multiplexer_3 (
    .in0(ula_1_out_4), .in1({out_2[3:0], 4'b0000}), .out(multiplexer_3_out),
    .sel(controle_1_sinal_de_controle[0]));

  // Notes on the sheet:
  //   r1
  //   r2
  //   cte
  //   Nome: Lucas Panonko Assis Belchior 12311BCC068
endmodule

module ULA (
  input  [7:0] DA,
  input  [7:0] DB,
  input  [2:0] Sel,
  output [7:0] out_4
);

  wire [7:0] adder_1_out, and_1_out, demultiplexer_1_out0, demultiplexer_1_out1, multiplexer_1_out,
       nor_1_out, not_1_out, or_1_out, xor_1_out;

  assign not_1_out = ~DB;  // NOT_Gate not_1, 8 bits wide
  Multiplexer #(.width(8), .enable("false")) multiplexer_1 (
    .in0(DB), .in1(not_1_out), .out(multiplexer_1_out), .sel(Sel[0]));
  assign and_1_out = DA & DB;  // AND_Gate and_1, 8 bits wide
  assign or_1_out = DA | DB;  // OR_Gate or_1, 8 bits wide
  assign nor_1_out = ~(DA | DB);  // NOR_Gate nor_1, 8 bits wide
  assign xor_1_out = DA ^ DB;  // XOR_Gate xor_1, 8 bits wide
  Demultiplexer #(.width(8), .enable("false")) demultiplexer_1 (
    .out0(demultiplexer_1_out0), .out1(demultiplexer_1_out1), .in(adder_1_out), .sel(Sel[0]));
  Adder adder_1 (.a(DA), .b(multiplexer_1_out), .out(adder_1_out), .cin(Sel[0]));  // open: cout
  Multiplexer #(.select(3), .width(8), .enable("false")) multiplexer_2 (
    .in0(demultiplexer_1_out0), .in1(demultiplexer_1_out1), .in2(and_1_out), .in3(or_1_out), .in4(nor_1_out),
    .in5(xor_1_out), .in6({8{1'b0}}), .in7({8{1'b0}}), .out(out_4), .sel(Sel));
endmodule

module Controle (
  input  [3:0] opcode,
  output [5:0] Sinal_de_controle
);

  Multiplexer #(.select(4), .width(6), .enable("false")) multiplexer_1 (
    .in0(6'b000100), .in1(6'b001100), .in2(6'b010100), .in3(6'b011100), .in4(6'b100100), .in5(6'b101100),
    .in6(6'b011110), .in7(6'b000111), .in8(6'b000111), .out(Sinal_de_controle), .sel(opcode));  // open: in9, in10, in11, in12, in13, in14, in15
endmodule

module Regs (
  input  [7:0] dRW,
  input  rw,
  input  [1:0] RW_2,
  input  CLK,
  input  [1:0] R1,
  input  [1:0] R2,
  output [7:0] dR1,
  output [7:0] dR2
);

  wire demultiplexer_1_out0, demultiplexer_1_out1, demultiplexer_1_out2, demultiplexer_1_out3;
  wire [7:0] A_q, B_q, C_q, D_q;

  Demultiplexer #(.select(2), .enable("false")) demultiplexer_1 (
    .out0(demultiplexer_1_out0), .out1(demultiplexer_1_out1), .out2(demultiplexer_1_out2),
    .out3(demultiplexer_1_out3), .in(rw), .sel(RW_2));
  Register #(.Select("low")) A (.D(dRW), .en(demultiplexer_1_out0), .Q(A_q), .clk(CLK));  // open: clr
  Register #(.Select("low")) B (.D(dRW), .en(demultiplexer_1_out1), .Q(B_q), .clk(CLK));  // open: clr
  Register #(.Select("low")) C (.D(dRW), .en(demultiplexer_1_out2), .Q(C_q), .clk(CLK));  // open: clr
  Register #(.Select("low")) D (.D(dRW), .en(demultiplexer_1_out3), .Q(D_q), .clk(CLK));  // open: clr
  Multiplexer #(.select(2), .width(8), .enable("false")) multiplexer_1 (
    .in0(A_q), .in1(B_q), .in2(C_q), .in3(D_q), .out(dR1), .sel(R1));
  Multiplexer #(.select(2), .width(8), .enable("false")) multiplexer_2 (
    .in0(A_q), .in1(B_q), .in2(C_q), .in3(D_q), .out(dR2), .sel(R2));
endmodule
